# Fritzing sketch bogen1 (saved by Fritzing 0.9.3b)
perfboards: 1

parts:
  Q1 = NPN-Transistor [package="TO92 [THT]"]
  Q2 = NPN-Transistor [package="TO92 [THT]"]
  Q3 = NPN-Transistor [package="TO92 [THT]"]
  LED1 = LED - 5mm [color="Red (633nm)" package="5 mm [THT]"]
  LED2 = LED - 5mm [color="Yellow (585nm)" package="5 mm [THT]"]
  LED3 = LED - 5mm [color="Green (560nm)" package="5 mm [THT]"]
  Raspberry_Pi_A1 = Raspberry Pi A
  Q4 = NPN-Transistor [package="TO92 [THT]"]
  IC1 = ULN2803A [package=THT]
  S2 = Square Pushbutton
  U1 = 4-Channel 5v Relay Shield [package=relay-4ch5v10a]
  R1 = Resistor [tolerance=±5% resistance=220 package="1206 [SMD]"]
  R2 = Resistor [tolerance=±5% resistance=220 package="1206 [SMD]"]
  R3 = Resistor [tolerance=±5% resistance=220 package="1206 [SMD]"]
  J1 = Piezo Speaker
  R4 = Resistor [tolerance=±5% resistance=220 package="1206 [SMD]"]

nets:
  N1: Q1.B, Raspberry_Pi_A1.GPIO_24
  N2: Q1.C, LED1.cathode
  N3: Q2.E, R2.Pin_0
  N4: Q2.C, LED2.cathode
  N5: Q3.E, R3.Pin_0
  N6: Q3.B, Raspberry_Pi_A1.GPIO_25
  N7: Q3.C, LED3.cathode
  GND: LED2.anode, Raspberry_Pi_A1.GND, U1.GND
  N8: LED3.anode, S2.leg0
  5V: Raspberry_Pi_A1.5V, Q4.E, U1.VCC, R1.Pin_1, R3.Pin_1
  N9: Raspberry_Pi_A1.GPIO_11, Q4.B
  N10: Raspberry_Pi_A1.GPIO_7, R4.Pin_1
  N11: Q4.C, J1.pin1
  N12: IC1.Out_5, U1.IN3
  N13: IC1.Out_3, U1.IN2
  N14: IC1.Out_1, U1.IN1
  N15: S2.leg1, R4.Pin_0

custom parts:
  4-Channel 5v Relay Shield: 4 Channel 5v Relay Shield w. 2x SPD-06VDC-SD-C
